# Fritzing sketch lab5 (saved by Fritzing 0.9.9b)
breadboards: 1

parts:
  Part1 = Arduino Uno (Rev3)
  LED1 = LED - 5mm [color="Red (633nm)" current=0.030 package="5 mm [THT]"]
  LED6 = LED - 5mm [color="Red (633nm)" current=0.030 package="5 mm [THT]"]
  LED7 = LED - 5mm [color="Yellow (595nm)" current=0.030 package="5 mm [THT]"]
  LED8 = LED - 5mm [color="Yellow (595nm)" current=0.030 package="5 mm [THT]"]
  LED9 = LED - 5mm [color="Green (565nm)" current=0.030 package="5 mm [THT]"]
  R1 = Resistor [tolerance=±5% power=0.25 resistance=220 package=THT]
  R2 = Resistor [tolerance=±5% power=0.25 resistance=220 package=THT]
  R3 = Resistor [tolerance=±5% power=0.25 resistance=220 package=THT]
  R4 = Resistor [tolerance=±5% power=0.25 resistance=220 package=THT]
  R5 = Resistor [tolerance=±5% power=0.25 resistance=220 package=THT]
  R6 = Trimmer Potentiometer [maximum_resistance=10kΩ package=THT]

nets:
  N1: Part1.A0, R6.wiper
  N2: Part1.D8, LED6.cathode, R2.Pin_0, R2.Pin_1
  N3: Part1.D9_PWM, LED7.cathode, R3.Pin_0, R3.Pin_1
  N4: Part1.D10_PWM/SS, LED8.cathode, R4.Pin_0, R4.Pin_1
  N5: Part1.D11_PWM/MOSI, LED9.cathode, R5.Pin_0, R5.Pin_1
  N6: Part1.D7, LED1.cathode, R1.Pin_0, R1.Pin_1
  N7: Part1.5V, R6.leg2
  N8: Part1.GND, LED1.anode, LED6.anode, LED7.anode, LED8.anode, LED9.anode, R6.leg1

notes:
  port 7
  port 8
  port 9
  port 10
  port 11
  The wires for the first 4 lights feed into another wire, which transmits the signal to the potentiometer's ground input.
  The wire for the last light instead connects to the potentiometer's line directly, due to lack of space.
  The potentiometer here takes 5V power, and outputs an analog signal depending on how far it's turned.
